// Logisim project AllLogisim2232058642LECLErC.circ as structural Verilog: 9 circuits, main circuit main
module main (
);

  SOM som_1 ();  // open: W, X, Y
  POM pom_1 ();  // open: W, X, Y
  SOP sop_1 ();  // open: W, X, Y
  POS pos_1 ();  // open: W, X, Y
  NANDSOP nandsop_1 ();  // open: w, x, y
  NORPOS norpos_1 ();  // open: W, X, Y
  MUX mux_1 ();  // open: W, X, Y
  DEC dec_1 ();  // open: W, X, Y
endmodule

module SOM (
  input  W,
  input  X,
  input  Y
);

  wire a_out, df_out, e_out, g_out, m0_out, m1_out, m2_out, m3_out, m4_out, m5_out, m6_out, not_1_out,
       not_2_out, not_3_out, or_1_out, or_2_out, or_3_out, or_4_out, or_5_out, or_6_out;

  not not_1 (not_1_out, W);
  not not_2 (not_2_out, X);
  not not_3 (not_3_out, Y);
  and m0 (m0_out, not_1_out, not_2_out, not_3_out);
  and m1 (m1_out, not_1_out, not_2_out, Y);
  and m2 (m2_out, not_1_out, X, not_3_out);
  and m3 (m3_out, not_1_out, X, Y);
  and m4 (m4_out, W, not_2_out, not_3_out);
  and m5 (m5_out, W, not_2_out, Y);
  and m6 (m6_out, W, X, not_3_out);
  or or_1 (or_1_out, m1_out, m2_out, m4_out);
  or or_2 (or_2_out, m0_out, m1_out, m2_out);
  or or_3 (or_3_out, m3_out, m4_out, m6_out);
  or or_4 (or_4_out, m0_out, m1_out, m2_out);
  or or_5 (or_5_out, m3_out, m4_out, m5_out);
  or or_6 (or_6_out, or_5_out, m6_out);
  or a (a_out, or_1_out, m6_out);
  or df (df_out, or_2_out, or_3_out);
  or e (e_out, or_4_out, or_6_out);
  or g (g_out, m1_out, m4_out, m5_out);
  _7_Segment_Display u_7_segment_display_1 (.g(g_out), .f(df_out), .a(a_out), .e(e_out), .d(df_out));  // open: b, c, dp

  // Notes on the sheet:
  //   m0
  //   m1
  //   m2
  //   m3
  //   m4
  //   m5
  //   m6
endmodule

module POM (
  input  W,
  input  X,
  input  Y
);

  wire a_out, and_1_out, and_2_out, and_3_out, bc_out, g_out, M0_out, M1_out, M2_out, M3_out, M4_out, M5_out,
       M6_out, not_1_out, not_2_out, not_3_out;

  not not_1 (not_1_out, W);
  not not_2 (not_2_out, X);
  not not_3 (not_3_out, Y);
  or M0 (M0_out, W, X, Y);
  or M1 (M1_out, W, X, not_3_out);
  or M2 (M2_out, W, not_2_out, Y);
  or M3 (M3_out, W, not_2_out, not_3_out);
  or M4 (M4_out, not_1_out, X, Y);
  or M5 (M5_out, not_1_out, X, not_3_out);
  or M6 (M6_out, not_1_out, not_2_out, Y);
  and and_1 (and_1_out, M0_out, M1_out, M2_out);
  and and_2 (and_2_out, M3_out, M4_out, M5_out);
  and and_3 (and_3_out, M0_out, M2_out, M3_out);
  and a (a_out, M0_out, M3_out, M5_out);
  and bc (bc_out, and_1_out, and_2_out, M6_out);
  and g (g_out, and_3_out, M6_out);
  _7_Segment_Display u_7_segment_display_1 (
    .g(g_out), .f(M5_out), .a(a_out), .b(bc_out), .e(1'b1), .d(M5_out), .c(bc_out));  // open: dp

  // Notes on the sheet:
  //   M0
  //   M1
  //   M2
  //   M3
  //   M4
  //   M5
  //   M6
  //   df
endmodule

module SOP (
  input  W,
  input  X,
  input  Y
);

  wire a_out, and_1_out, and_2_out, df_out, g_out, not_1_out, not_2_out, not_3_out, or_1_out, or_2_out,
       or_3_out;

  not not_1 (not_1_out, W);
  not not_2 (not_2_out, X);
  not not_3 (not_3_out, Y);
  or or_1 (or_1_out, W, X, Y);
  or or_2 (or_2_out, not_2_out, not_3_out);
  and a (a_out, or_1_out, or_2_out, or_3_out);
  or or_3 (or_3_out, not_1_out, not_3_out);
  or df (df_out, not_1_out, not_3_out);
  and and_1 (and_1_out, not_2_out, Y);
  or g (g_out, and_1_out, and_2_out);
  and and_2 (and_2_out, W, not_2_out);
  _7_Segment_Display u_7_segment_display_1 (.g(g_out), .f(df_out), .a(a_out), .e(1'b1), .d(df_out));  // open: b, c, dp

  // Notes on the sheet:
  //   e
endmodule

module POS (
  input  W,
  input  X,
  input  Y
);

  wire a_out, df_out, g_out, not_1_out, not_2_out, not_3_out, or_1_out, or_2_out, or_3_out, or_4_out,
       or_5_out, or_6_out;

  not not_1 (not_1_out, W);
  not not_2 (not_2_out, X);
  not not_3 (not_3_out, Y);
  or or_1 (or_1_out, W, X, Y);
  or or_2 (or_2_out, W, not_2_out, not_3_out);
  or or_3 (or_3_out, not_1_out, X, not_3_out);
  or df (df_out, not_1_out, not_3_out);
  or or_4 (or_4_out, not_2_out, Y);
  or or_5 (or_5_out, W, not_2_out);
  or or_6 (or_6_out, W, Y);
  and a (a_out, or_1_out, or_2_out, or_3_out);
  and g (g_out, or_4_out, or_5_out, or_6_out);
  _7_Segment_Display u_7_segment_display_1 (.g(g_out), .f(df_out), .a(a_out), .e(1'b1), .d(df_out));  // open: b, c, dp
endmodule

module NANDSOP (
  input  w,
  input  x,
  input  y
);

  wire a_out, df_out, g_out, nand_1_out, nand_2_out, nand_3_out, nand_4_out, nand_5_out, nand_6_out,
       nand_7_out, nand_8_out, nand_9_out;

  nand nand_1 (nand_1_out, w, w);
  nand nand_2 (nand_2_out, x, x);
  nand nand_3 (nand_3_out, y, y);
  nand nand_4 (nand_4_out, nand_1_out, nand_2_out, nand_3_out);
  nand nand_5 (nand_5_out, x, y);
  nand nand_6 (nand_6_out, w, y);
  nand df (df_out, w, y);
  nand nand_7 (nand_7_out, nand_2_out, y);
  nand nand_8 (nand_8_out, w, nand_2_out);
  nand nand_9 (nand_9_out, nand_4_out, nand_5_out, nand_6_out);
  nand g (g_out, nand_7_out, nand_8_out);
  nand a (a_out, nand_9_out, nand_9_out);
  _7_Segment_Display u_7_segment_display_1 (.g(g_out), .f(df_out), .a(a_out), .e(1'b1), .d(df_out));  // open: b, c, dp

  // Notes on the sheet:
  //   e
endmodule

module NORPOS (
  input  W,
  input  X,
  input  Y
);

  wire a_out, df_out, g_out, nor_1_out, nor_2_out, nor_3_out, nor_4_out, nor_5_out, nor_6_out, nor_7_out,
       nor_8_out, nor_9_out, nor_10_out;

  nor nor_1 (nor_1_out, W, W);
  nor nor_2 (nor_2_out, X, X);
  nor nor_3 (nor_3_out, Y, Y);
  nor nor_4 (nor_4_out, W, X, Y);
  nor nor_5 (nor_5_out, W, nor_2_out, nor_3_out);
  nor nor_6 (nor_6_out, nor_1_out, X, nor_3_out);
  nor nor_7 (nor_7_out, nor_1_out, nor_3_out);
  nor nor_8 (nor_8_out, nor_2_out, Y);
  nor nor_9 (nor_9_out, W, nor_2_out);
  nor nor_10 (nor_10_out, W, Y);
  nor a (a_out, nor_4_out, nor_5_out, nor_6_out);
  nor df (df_out, nor_7_out, nor_7_out);
  nor g (g_out, nor_8_out, nor_9_out, nor_10_out);
  _7_Segment_Display u_7_segment_display_1 (.g(g_out), .f(df_out), .a(a_out), .e(1'b1), .d(df_out));  // open: b, c, dp
endmodule

module MUX (
  input  W,
  input  X,
  input  Y
);

  wire multiplexer_1_out, multiplexer_2_out, multiplexer_3_out, not_1_out;

  not not_1 (not_1_out, Y);
  Multiplexer #(.select(2)) multiplexer_1 (
    .in0(Y), .in1(not_1_out), .in2(not_1_out), .in3(not_1_out), .out(multiplexer_1_out), .sel({W, X}));
  Multiplexer #(.select(2)) multiplexer_2 (
    .in0(1'b1), .in1(1'b1), .in2(not_1_out), .in3(not_1_out), .out(multiplexer_2_out), .sel({W, X}));
  Multiplexer #(.select(2)) multiplexer_3 (
    .in0(Y), .in1(1'b0), .in2(1'b1), .in3(Y), .out(multiplexer_3_out), .sel({W, X}));
  _7_Segment_Display u_7_segment_display_1 (
    .g(multiplexer_3_out), .f(multiplexer_2_out), .a(multiplexer_1_out), .e(1'b1), .d(multiplexer_2_out));  // open: b, c, dp

  // Notes on the sheet:
  //   A
  //   DF
  //   G
endmodule

module DEC (
  input  W,
  input  X,
  input  Y
);

  wire a_out, decoder_1_out0, decoder_1_out1, decoder_1_out2, decoder_1_out3, decoder_1_out4, decoder_1_out5,
       decoder_1_out6, df_out, g_out, or_1_out, or_2_out, or_3_out;

  Decoder #(.select(3)) decoder_1 (
    .out0(decoder_1_out0), .out1(decoder_1_out1), .out2(decoder_1_out2), .out3(decoder_1_out3),
    .out4(decoder_1_out4), .out5(decoder_1_out5), .out6(decoder_1_out6), .sel({W, X, Y}));  // open: out7, en
  or or_1 (or_1_out, decoder_1_out1, decoder_1_out2, decoder_1_out4);
  or or_2 (or_2_out, decoder_1_out0, decoder_1_out1, decoder_1_out2);
  or or_3 (or_3_out, decoder_1_out3, decoder_1_out4, decoder_1_out6);
  or g (g_out, decoder_1_out1, decoder_1_out4, decoder_1_out5);
  or a (a_out, or_1_out, decoder_1_out6);
  or df (df_out, or_2_out, or_3_out);
  _7_Segment_Display u_7_segment_display_1 (.g(g_out), .f(df_out), .a(a_out), .e(1'b1), .d(df_out));  // open: b, c, dp
endmodule
