// Logisim project Sequential2232058642.circ as structural Verilog
module TCounter (
  output Qa,
  output Qb,
  output Qc
);

  wire and_1_out, and_2_out, clock_1_out, or_1_out;

  Clock clock_1 (.out(clock_1_out));
  and and_1 (and_1_out, Qb, Qa);
  and and_2 (and_2_out, Qb, Qc);
  T_Flip_Flop Ta (.T(1'b1), .clk(clock_1_out), .Q(Qa));  // open: Qn, reset, preset
  T_Flip_Flop Tb (.T(Qa), .clk(clock_1_out), .Q(Qb));  // open: Qn, reset, preset
  or or_1 (or_1_out, and_1_out, and_2_out);
  T_Flip_Flop Tc (.T(or_1_out), .clk(clock_1_out), .Q(Qc));  // open: Qn, reset, preset
endmodule

module DCounter (
  output Qa,
  output Qb,
  output Qc
);

  wire and_1_out, and_2_out, and_3_out, and_4_out, and_5_out, and_6_out, clock_1_out, Da_qn, Db_qn, Dc_qn,
       or_1_out, or_2_out, or_3_out;

  Clock clock_1 (.out(clock_1_out));
  D_Flip_Flop Da (.D(or_1_out), .clk(clock_1_out), .Q(Qa), .Qn(Da_qn));  // open: preset, reset
  D_Flip_Flop Db (.D(or_2_out), .clk(clock_1_out), .Q(Qb), .Qn(Db_qn));  // open: preset, reset
  D_Flip_Flop Dc (.D(or_3_out), .clk(clock_1_out), .Q(Qc), .Qn(Dc_qn));  // open: preset, reset
  and and_1 (and_1_out, Da_qn, Dc_qn);
  and and_2 (and_2_out, Db_qn, Da_qn);
  or or_1 (or_1_out, and_1_out, and_2_out);
  and and_3 (and_3_out, Qa, Db_qn);
  and and_4 (and_4_out, Dc_qn, Da_qn, Qb);
  and and_5 (and_5_out, Qb, Qa);
  and and_6 (and_6_out, Db_qn, Qc);
  or or_2 (or_2_out, and_3_out, and_4_out);
  or or_3 (or_3_out, and_5_out, and_6_out);
endmodule

module JKCounter (
  output Qa,
  output Qb,
  output Qc
);

  wire and_1_out, clock_1_out, JKb_qn, JKc_qn, or_1_out, or_2_out;

  Clock clock_1 (.out(clock_1_out));
  or or_1 (or_1_out, JKb_qn, JKc_qn);
  or or_2 (or_2_out, Qa, Qc);
  and and_1 (and_1_out, Qb, Qa);
  J_K_Flip_Flop JKa (.J(or_1_out), .K(1'b1), .clk(clock_1_out), .Q(Qa));  // open: Qn, preset, reset
  J_K_Flip_Flop JKb (.J(Qa), .K(or_2_out), .clk(clock_1_out), .Q(Qb), .Qn(JKb_qn));  // open: preset, reset
  J_K_Flip_Flop JKc (.J(and_1_out), .K(Qa), .clk(clock_1_out), .Q(Qc), .Qn(JKc_qn));  // open: preset, reset
endmodule
